# Fritzing sketch wiring (saved by Fritzing 1.0.2b)
breadboards: 1

parts:
  IRLZ44N = MOSFET-NCHANNEL [package=to220v]
  R2 = Resistor [tolerance=±1% resistance=1k power=0.25W package=THT]
  C1 = Electrolytic Capacitor [capacitance=0.1mF voltage=20V package="100 mil [THT, electrolytic]"]
  V1 = DC Power [voltage=12V]
  Raspberry_Pi_4 = Raspberry Pi B+
  USB-C = USB Connectors [package=usb-a-h]
  Motor_Power = DC Power [voltage=12V]
  LED_Ring = NeoPixel Jewel [part_number=2226]
  C2 = Capacitor Polarized [mn=100uF package=panasonic_d]
  NEMA17 = Stepper Motor - Bipolar [mn=40-42]
  Motor_Power1 = DC Power [voltage=12V]
  C3 = Capacitor Polarized [mn=100uF package=panasonic_d]
  DRV_2 = DRV 8825 Stepper Motor Carrier, High Current [part_number="DRV 8825"]
  USB-C1 = USB Connectors [package=usb-a-h]
  NEMA18 = Stepper Motor - Bipolar [mn=40-42]
  part = TMC2209 [package=THT]

nets:
  N1: IRLZ44N.G, R2.Pin_1
  N2: IRLZ44N.D, LED_Ring.GND
  N3: IRLZ44N.S, C1.-, V1.V-
  N4: R2.Pin_0, Raspberry_Pi_4.GPIO18
  N5: C1.+, V1.V+
  N6: USB-C.VBUS, Motor_Power.V+, C2.+, part.VM
  GND: USB-C.GND, Motor_Power.V-, part.GND
  N7: NEMA17.A, part.M1B
  N8: NEMA17.C, part.M1A
  N9: NEMA17.B, part.M2A
  N10: NEMA17.D, part.M2B
  N11: Motor_Power1.V+, C3.+, DRV_2.VOLTAGE_ST/_MT, USB-C1.VBUS
  N12: Motor_Power1.V-, C3.-, DRV_2.GROUND_ST/_MT, DRV_2.GROUND_LOG, USB-C1.GND
  N13: DRV_2.RESET, DRV_2.SLEEP
  net label: DRV_2.STEP, DRV_2.DIRECTION
  N14: DRV_2.OUT_2B, NEMA18.A
  N15: DRV_2.OUT_2A, NEMA18.C
  N16: DRV_2.OUT_1A, NEMA18.B
  N17: DRV_2.OUT_1B, NEMA18.D
  3.3v: part.VIO, part.EN
  GPIO: part.Dir, part.Step

custom parts:
  NeoPixel Jewel: We fit seven of our tiny 5050 (5mm x 5mm) smart RGB LEDs onto a beautiful, round PCB with mounting holes and a chainable design to create what we think is our most elegant (and evening-wear appropriate) NeoPixel board yet. Use only one microcontroller pin to control as many as you can chain together! Each LED is addressable as the driver chip is inside the LED. Each one has ~18mA constant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
  TMC2209: TMC2209-LA stepper motor controller and driver. Supply voltage 4.75-28V Iphase up to 1.77A rms (2.5A peak)
