# Fritzing sketch wiring (saved by Fritzing 0.9.3b)
breadboards: 1

parts:
  IRLZ44N = MOSFET-NCHANNEL [package=to220v]
  R2 = Resistor [tolerance=±1% resistance=1k package=THT]
  C1 = Electrolytic Capacitor [capacitance=0.1mF voltage=20V package="100 mil [THT, electrolytic]"]
  V1 = DC Power [voltage=12V]
  Raspberry_Pi_4 = Raspberry Pi B+
  LED_Ring = NeoPixel Jewel [part_number=2226]

nets:
  N1: IRLZ44N.G, R2.Pin_1
  N2: IRLZ44N.D, LED_Ring.GND
  N3: IRLZ44N.S, C1.-, V1.V-
  N4: R2.Pin_0, Raspberry_Pi_4.GPIO18
  N5: C1.+, V1.V+

custom parts:
  NeoPixel Jewel: We fit seven of our tiny 5050 (5mm x 5mm) smart RGB LEDs onto a beautiful, round PCB with mounting holes and a chainable design to create what we think is our most elegant (and evening-wear appropriate) NeoPixel board yet. Use only one microcontroller pin to control as many as you can chain together! Each LED is addressable as the driver chip is inside the LED. Each one has ~18mA constant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
